# Fritzing sketch ESPfig (saved by Fritzing 0.9.5d)
breadboards: 1

parts:
  U1 = ESP32S-HiLetgo [part_number=ESP32S-HiLetgo]
  パーツ1 = Breakout Board for Electret Microphone
  LED1 = LED - 5mm [color="Red (633nm)" package="5 mm [THT]"]

nets:
  N1: U1.3.3, パーツ1.AUD
  N2: U1.GPIO25, パーツ1.VCC
  N3: U1.GPIO26, LED1.anode
  N4: U1.GND, LED1.cathode

notes:
  マイクアンプキットは左から
  Vout
  GND
  VCC
  26番PIN --- LEDの+
  25番PIN --- マイクアンプのVout
  3.3V --- マイクのVcc
  GND --- LEDの- マイクのGND

custom parts:
  ESP32S-HiLetgo: HiLetgo ESP-WROOM-32 ESP32 ESP-32S Development Board 2.4GHz Dual-Mode WiFi + Bluetooth Dual Cores Microcontroller The ESP32 integrated with Antenna switches, RF Balun, power amplifiers, low-noise amplifiers, filters, and management modules, and the entire solution occupies the least area of PCB. 2.4 GHz Wi-Fi plus Bluetooth dual-mode chip, with TSMC Ultra-low power consumption 40nm technology,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
